# Fritzing sketch Enregistreur Qualité de l'air (saved by Fritzing 0.9.3b)
circuit board: 10.5031cm x 7.71316cm
breadboards: 1

parts:
  DHT1 = DHT22 Humidity and Temperature Sensor
  R1 = Resistor [tolerance=±5% resistance=4.7k package="2512 [SMD]"]
  IC1 = iAQ-core [package=THT]
  C1 = Capacitor [part_number=100n package=cap-pth-small2]
  IC2 = Arduino Mega 2560 (Rev3)

nets:
  VDD: DHT1.VDD, R1.Pin_0, IC1.+3V3, C1.2, IC2.3V3
  N1: DHT1.DATA, R1.Pin_1, IC2.D2_PWM
  GND: DHT1.NULL, IC1.GND, C1.1, IC2.GND
  N2: IC1.SDA_-_I2C_Data, IC2.D20/SDA, IC2.SDA
  N3: IC1.SCL_-_I2C_Clock, IC2.D21/SCL, IC2.SCL

notes:
  [Montage qui permet de mesurer la qualité de l'air :
  Humidité en %
  Température en °C
  CO2 en PPM
  TVOC en PPB
  Sortie RS232 sur port USB]
  Connexion vers USB PC nécessaire

custom parts:
  iAQ-core: Air quality sensor
  Capacitor: Capacitor Standard 0603 ceramic capacitor, and 0.1 leaded capacitor.
